# Fritzing sketch pcb-2 (saved by Fritzing 0.9.10b)
stripboards: 1

parts:
  Mod1 = Raspberry Pi 4B  # not connected
  J1 = female pin header, 2 pins [form="♀ (female)"]
  J2 = female pin header, 2 pins [form="♀ (female)"]
  J3 = female pin header, 2 pins [form="♀ (female)"]
  J4 = female pin header, 2 pins [form="♀ (female)"]
  J5 = female pin header, 2 pins [form="♀ (female)"]
  J6 = female pin header, 2 pins [form="♀ (female)"]
  J7 = female pin header, 2 pins [form="♀ (female)"]
  J8 = female pin header, 2 pins [form="♀ (female)"]
  J9 = female pin header, 2 pins [form="♀ (female)"]
  J10 = female pin header, 2 pins [form="♀ (female)"]
  J11 = female pin header, 2 pins [form="♀ (female)"]
  J12 = female pin header, 2 pins [form="♀ (female)"]  # not connected
  J13 = Buzzer  # not connected
  J14 = female pin header, 2 pins [form="♀ (female)"]
  J15 = female pin header, 2 pins [form="♀ (female)"]
  J16 = female pin header, 2 pins [form="♀ (female)"]  # not connected
  J17 = female pin header, 2 pins [form="♀ (female)"]
  J18 = female pin header, 2 pins [form="♀ (female)"]
  J19 = female pin header, 2 pins [form="♀ (female)"]
  J20 = female pin header, 2 pins [form="♀ (female)"]
  J21 = female pin header, 2 pins [form="♀ (female)"]
  J22 = female pin header, 2 pins [form="♀ (female)"]
  J23 = female pin header, 2 pins [form="♀ (female)"]
  J24 = female pin header, 2 pins [form="♀ (female)"]
  J25 = female pin header, 2 pins [form="♀ (female)"]
  R1 = Resistor [tolerance=±5% resistance=220 package="0402 [SMD]"]
  J26 = female pin header, 2 pins [form="♀ (female)"]
  J27 = female pin header, 2 pins [form="♀ (female)"]
  J28 = female pin header, 2 pins [form="♀ (female)"]
  J29 = female pin header, 2 pins [form="♀ (female)"]
  J30 = female pin header, 2 pins [form="♀ (female)"]
  J31 = female pin header, 2 pins [form="♀ (female)"]
  R2 = Resistor [tolerance=±5% power=0.25 resistance=220 package=THT]

nets:
  N1: J1.pin1, J3.pin1, J5.pin1, J7.pin1, J9.pin1, J14.pin1, J17.pin2, J18.pin2, J19.pin2, J28.pin2, J29.pin2, J30.pin2, J31.pin2, R2.Pin_0
  N2: J1.pin2, J3.pin2, J5.pin2, J7.pin2, J9.pin2, J10.pin1, R1.Pin_0
  N3: J2.pin1, J4.pin1, J6.pin1, J8.pin1
  N4: J2.pin2, J4.pin2, J6.pin2, J8.pin2
  N5: J10.pin2, R1.Pin_1
  N6: J11.pin1, J28.pin1, J29.pin1, J30.pin1, J31.pin1
  N7: J14.pin2, J15.pin1, J17.pin1, J18.pin1, J19.pin1, J26.pin2
  N8: J20.pin1, J21.pin1, J22.pin1
  N9: J20.pin2, J23.pin1
  N10: J21.pin2, J24.pin1
  N11: J22.pin2, J25.pin1
  N12: J23.pin2, J24.pin2, J25.pin2
  N13: J26.pin1, J27.pin2, R2.Pin_1

notes:
  OneWire
  Gnd|3.3V|W
  DS18B20
  I²C
  5V|Gnd|3.3V|SDA|CLK
  SH31, LCD/OLED
  Switch+LED
  GPIO|GPIO|3.3V
  BCM: 27|22|3V
  Rotary + push
  Gnd|3.3V|GPIO|GPIO|GPIO
  BCM: G|3V|0|5|6
  SPI
  3.3V|Gnd|DO|CS|CL
  MAX31855
  Bus 1 Channel 1
  Bus 1 Channel 0
  Bus 1 Channel 2
  Valve Relays
  5V|Gnd|GPIO|GPIO
  !! Low active relays
  => gpio=23=ip,dh
  => gpio=24=ip,dh

custom parts:
  Buzzer: Fixed frequency buzzer
